# Fritzing sketch HumanCounter (saved by Fritzing 0.9.3b)
breadboards: 2

parts:
  부품1 = Arduino Yun
  PIR1 = PIR sensor
  부품2 = Bluetooth HC-05 Macho
  부품3 = Arduino Mega 2560 (Rev3)
  부품4 = Bluetooth HC-05 Macho
  J2 = Piezo Speaker
  U7 = 7-SEGMENT-4DIGIT [package=7-segment-4digit]

nets:
  N1: 부품1.D2, PIR1.SIG
  N2: 부품1.D4, 부품2.TXD
  N3: 부품1.D5_PWM, 부품2.RXD
  VDD: PIR1.VDD, 부품2.VCC
  GND: PIR1.GND, 부품2.GND
  N4: 부품3.D19/RX1, 부품4.TXD
  N5: 부품3.D18/TX1, 부품4.RXD
  GND_2: 부품3.GND, 부품4.GND, J2.pin1
  N6: 부품3.D3_PWM, J2.pin2
  N7: 부품3.D31, 부품3.D37, 부품3.D39, 부품3.D41, U7.1, U7.2, U7.3, U7.4
  N8: 부품3.D33, U7.5
  N9: 부품3.D35, 부품3.D45, 부품3.D47, 부품3.D51, U7.13, U7.14, U7.15, U7.16
  N10: 부품3.D43, U7.8, U7.9
  N11: 부품3.D49, U7.6
  N12: 부품3.D53, U7.11
